# Fritzing sketch aufbau (saved by Fritzing 0.9.3b)
circuit board: 5.42188cm x 4.95904cm
breadboards: 1

parts:
  U3 = NodeMCU V1.0
  Bauteil1 = Adafruit BMP180
  LED1 = RGB LED (com. cathode, rgb) [package="5 mm [THT]"]

nets (from the breadboard view):
  N1: U3.D0, U3.RST
  N2: U3.D1, LED1.green_anode
  N3: U3.D2, LED1.blue_anode
  N4: U3.D3, Bauteil1.SCL
  N5: U3.D4, Bauteil1.SDA
  3V3: U3.3V3, Bauteil1.+3V3
  GND: U3.GND, Bauteil1.GND, LED1.common_cathode
  N6: U3.D5, LED1.red_anode

notes:
  A16 to RST for deep Sleep Mode

custom parts:
  NodeMCU V1.0: ESP8266 based NodeMCU
  Adafruit BMP180: This precision sensor from Bosch is the best low-cost sensing solution for measuring barometric pressure and temperature. Because pressure changes with altitude you can also use it as an altimeter! The sensor is soldered onto a PCB with a 3.3V regulator, I2C level shifter and pull-up resistors on the I2C pins. The BMP180 is the next-generation of sensors from Bosch, and replaces the BMP085.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
